// Logisim project PROGRAM17.circ as structural Verilog: 1 circuit, main circuit main
module main (
  input  in_1,
  input  in_2
);

  wire and_1_out, t_ff_1_q, t_ff_2_q, t_ff_3_q;

  T_Flip_Flop t_ff_1 (.clk(in_2), .T(in_1), .Q(t_ff_1_q));  // open: Qn, preset, reset, en
  LED led_1 ();  // open: in
  LED led_2 ();  // open: in
  T_Flip_Flop t_ff_2 (.clk(in_2), .T(t_ff_1_q), .Q(t_ff_2_q));  // open: Qn, preset, reset, en
  and and_1 (and_1_out, t_ff_1_q, t_ff_2_q);
  LED led_3 ();  // open: in
  T_Flip_Flop t_ff_3 (.clk(in_2), .T(and_1_out), .Q(t_ff_3_q));  // open: Qn, preset, reset, en
endmodule
